# Fritzing sketch 001_tresLedBoton (saved by Fritzing 0.9.3b)
breadboards: 1

parts:
  Componente1 = Arduino Mega 2560 (Rev3)
  LED1 = smd LED [color="Red (633nm)" package="1206 [SMD]"]
  LED2 = smd LED [color="Red (633nm)" package="1206 [SMD]"]
  LED3 = smd LED [color="Red (633nm)" package="1206 [SMD]"]
  R1 = Resistor [tolerance=±5% resistance=330 package="2512 [SMD]"]
  R2 = Resistor [tolerance=±5% resistance=330 package="2512 [SMD]"]
  R3 = Resistor [tolerance=±5% resistance=330 package="2512 [SMD]"]
  S1 = Pushbutton [package="[THT]"]
  R4 = Resistor [tolerance=±5% resistance=220 package=THT]

nets:
  N1: Componente1.D8_PWM, R4.Pin_1
  N2: Componente1.5V, S1.Pin_3, S1.Pin_4
  N3: Componente1.GND, LED1.cathode, LED2.cathode, LED3.cathode, S1.Pin_1, S1.Pin_2, R4.Pin_0
  N4: Componente1.D2_PWM, R3.Pin_1
  N5: Componente1.D3_PWM, R2.Pin_1
  N6: Componente1.D4_PWM, R1.Pin_1
  N7: LED1.anode, R1.Pin_0
  N8: LED2.anode, R2.Pin_0
  N9: LED3.anode, R3.Pin_0

// code stored in the sketch: 001_tresLedBoton.ino
/* EN ESTE SENCILLO PROGRAMA PRENDO TRES LED
CONSECUTIVAMENTE HASTA QUE PRENDO LAS TRES Y RESETEO.
Se usa un botón y tres led. 
*/

int sCuenta = 0;
int sMaximo = 3;
int pinSestado = 0;
int tiempo = 3000;

const int pinS = 8; //i3
int pinBOMBILLA1 = 2; // q0
int pinBOMBILLA2 = 3; // q0
int pinBOMBILLA3 = 4; // q0


void setup(){
  
  pinMode(pinS, INPUT);// Declaro la entrada.
  pinMode(pinBOMBILLA1, OUTPUT); // Declaro la salida
  pinMode(pinBOMBILLA2, OUTPUT); // Declaro la salida
  pinMode(pinBOMBILLA3, OUTPUT); // Declaro la salida
   
  }
  

void loop(){
  Serial.begin(9600);
  pinSestado = digitalRead(pinS);
  if(pinSestado == HIGH){
    
    	for(sCuenta; sCuenta <= sMaximo; sCuenta++){
          //Serial.println(sCuenta);
          if(sCuenta==1){
            digitalWrite(pinBOMBILLA1, HIGH);
            digitalWrite(pinBOMBILLA2, LOW);
            digitalWrite(pinBOMBILLA3, LOW);
            Serial.println(sCuenta);
            delay(tiempo);
            Serial.println("hola");
            
            //while (Serial.available() <=0){}; // este codigo le da un descanso. No funciona en simulación, sí en arduino.
          }else if(sCuenta==2){
            digitalWrite(pinBOMBILLA2, HIGH);
            digitalWrite(pinBOMBILLA1, LOW);
            digitalWrite(pinBOMBILLA3, LOW);
            Serial.println(sCuenta);
            
            //while (Serial.available() <=0){}; // este codigo le da un descanso. No funciona en simulación, sí en arduino.
            delay(tiempo);
            //sCuenta = sCuenta++;
          }else if(sCuenta==3){
            digitalWrite(pinBOMBILLA1, HIGH);
            digitalWrite(pinBOMBILLA2, HIGH);
            digitalWrite(pinBOMBILLA3, HIGH);
            Serial.println(sCuenta);
            //while (Serial.available() <=0){}; // este codigo le da un descanso. No funciona en simulación, sí en arduino.
            delay(tiempo);
            sCuenta =0;
          }
        }
    
    
  }else{
    digitalWrite(pinBOMBILLA1, LOW);
    digitalWrite(pinBOMBILLA2, LOW);
    digitalWrite(pinBOMBILLA3, LOW);
    delay(tiempo);
  }
}
    
    
  }else{
    digitalWrite(pinBOMBILLA1, LOW);
    digitalWrite(pinBOMBILLA2, LOW);
    digitalWrite(pinBOMBILLA3, LOW);
    delay(tiempo);
  }
}
