# Fritzing sketch pap-botones-inversion-giro (saved by Fritzing 0.9.3b)
breadboards: 1

parts:
  MOTOR2 = 28BYJ-48 Stepper Motor
  X2 = X113647 Stepper Driver Board [package=board]
  Componente1 = Arduino Mega 2560 (Rev3)
  S1 = Momentary Switch [package=ksa_sealed_tac_switch]
  S2 = Momentary Switch [package=ksa_sealed_tac_switch]
  R1 = Resistor [tolerance=±5% resistance=220 package="2512 [SMD]"]
  R2 = Resistor [tolerance=±5% resistance=220 package="1206 [SMD]"]
  LED1 = smd LED [color="Red (633nm)" package="1206 [SMD]"]
  LED2 = smd LED [color="Red (633nm)" package="1206 [SMD]"]
  R3 = Resistor [tolerance=±5% resistance=220 package="0805 [SMD]"]
  R4 = Resistor [tolerance=±5% resistance=220 package="0805 [SMD]"]

nets:
  N1: MOTOR2.BLUE, X2.RED
  N2: MOTOR2.PINK, X2.ORANGE
  N3: MOTOR2.RED, X2.YELLOW
  N4: MOTOR2.ORANGE, X2.PINK
  N5: MOTOR2.YELLOW, X2.BLUE
  N6: X2.IN1, Componente1.D7_PWM
  N7: X2.IN2, Componente1.D6_PWM
  N8: X2.IN3, Componente1.D5_PWM
  N9: X2.IN4, Componente1.D4_PWM
  GND: X2.GND, Componente1.GND, R1.Pin_0, R2.Pin_0, R3.Pin_0, R4.Pin_0
  N10: X2.+V, Componente1.5V, S1.2, S2.2
  N11: Componente1.D11_PWM, LED2.anode
  N12: Componente1.D10_PWM, LED1.anode
  N13: Componente1.D9_PWM, S1.3, R2.Pin_1
  N14: Componente1.D8_PWM, S2.3, R1.Pin_1
  N15: LED1.cathode, R3.Pin_1
  N16: LED2.cathode, R4.Pin_1

custom parts:
  28BYJ-48 Stepper Motor: 28BYJ-48 gear-reduction stepper motor (small)
  X113647 Stepper Driver Board: A common stepper motor driver board based on ULN2003APG darlington array

// code stored in the sketch: pap-botones-inversion-giro.ino
#include <Stepper.h>

Stepper motor(2048, 4, 6, 5, 7);
int derechaB = 3;
int izquierdaB = 9;
int estadoBotonD;
int estadoBotonI;
int led =8;
int tiempo = 1000;
int demora = 11;   		// demora entre pasos, no debe ser menor a 10 ms.


void setup() {
  Serial.begin(9600);
  
  pinMode(derechaB, INPUT);		// todos los pines como salida
  pinMode(izquierdaB, INPUT);
   
  pinMode(derechaB, LOW);
  pinMode(izquierdaB, LOW);
  
  pinMode(led, OUTPUT);
  
  motor.setSpeed(10); // en RPM valores 1,2,3 para 28BYJ-48
}

void loop() {
  int estadoBotonD=digitalRead(derechaB);
  int estadoBotonI=digitalRead(izquierdaB);
  
         if(estadoBotonD == HIGH){
    
        digitalWrite(led,HIGH);
        motor.step(2048); // cantidad de pasos.
        delay(tiempo);
    
      } if (estadoBotonI == HIGH){
        
        digitalWrite(led,LOW);
        motor.step(-2048); // cantidad de pasos.
        delay(tiempo);
        
    }if ((estadoBotonD == HIGH) && (estadoBotonI == HIGH)){
      
      Serial.println("Error");
  }
}
